// Logisim project exo1.circ as structural Verilog: 1 circuit, main circuit main
module main (
  input  e0,
  input  e1,
  input  e2,
  output out_4
);

  wire CAS1_out, CAS2_out, CAS3_out, not_1_out, not_2_out, not_3_out;

  not not_1 (not_1_out, e0);
  not not_2 (not_2_out, e1);
  not not_3 (not_3_out, e2);
  and CAS1 (CAS1_out, e2, e1, not_1_out);
  and CAS2 (CAS2_out, e2, not_2_out, e0);
  and CAS3 (CAS3_out, not_3_out, e0, e1);
  or SORTIE (out_4, CAS2_out, CAS1_out, CAS3_out);
endmodule
