// Logisim project exo3.circ as structural Verilog: 1 circuit, main circuit main
module main (
  input  E0,
  input  E1,
  input  E2,
  input  E3,
  output out_5
);

  wire _0000_out, _0101_out, _1010_out, _1111_out, not_1_out, not_2_out, not_3_out, not_4_out;

  not not_1 (not_1_out, E0);
  not not_2 (not_2_out, E1);
  not not_3 (not_3_out, E2);
  not not_4 (not_4_out, E3);
  and _0000 (_0000_out, not_1_out, not_2_out, not_3_out, not_4_out);
  and _1010 (_1010_out, E0, not_2_out, E2, not_4_out);
  and _0101 (_0101_out, not_1_out, E1, not_3_out, E3);
  and _1111 (_1111_out, E0, E1, E2, E3);
  or or_1 (out_5, _0000_out, _1010_out, _0101_out, _1111_out);
endmodule
