// Logisim project exo1.circ as structural Verilog: 1 circuit, main circuit main
module main (
);

  wire a_b_out, a_c_d_out, a_c_nd_out, a_nb_nc_out, a_nb_nd_out, a_nc_d_out, a_nc_nd_out, button_1_out,
       d_ff_1_q, d_ff_2_q, d_ff_3_q, d_ff_4_q, na_b_out, na_c_d_out, na_c_out, na_d_out, not_1_out,
       not_2_out, not_3_out, not_4_out, or_1_out, or_2_out, or_3_out, or_4_out, undriven;

  Button button_1 (.out(button_1_out));
  D_Flip_Flop d_ff_1 (.clk(button_1_out), .Q(d_ff_1_q), .preset(undriven));  // open: D, Qn, en, reset
  D_Flip_Flop d_ff_2 (.clk(button_1_out), .D(or_1_out), .Q(d_ff_2_q));  // open: Qn, preset, en, reset
  D_Flip_Flop d_ff_3 (.clk(button_1_out), .D(or_2_out), .Q(d_ff_3_q));  // open: Qn, preset, en, reset
  D_Flip_Flop d_ff_4 (.clk(button_1_out), .Q(d_ff_4_q), .reset(or_3_out));  // open: D, Qn, preset, en
  not not_1 (not_1_out, d_ff_1_q);
  not not_2 (not_2_out, d_ff_2_q);
  not not_3 (not_3_out, d_ff_3_q);
  not not_4 (not_4_out, d_ff_4_q);
  and a_c_d (a_c_d_out, d_ff_1_q, d_ff_3_q, d_ff_4_q);
  or or_1 (or_1_out, a_c_d_out, a_b_out);
  and a_b (a_b_out, d_ff_1_q, d_ff_2_q);
  and a_nb_nc (a_nb_nc_out, d_ff_1_q, not_2_out, not_3_out);
  and a_nb_nd (a_nb_nd_out, d_ff_1_q, not_2_out, not_4_out);
  or or_2 (or_2_out, a_nb_nc_out, a_nb_nd_out, na_b_out);
  and na_b (na_b_out, not_1_out, d_ff_2_q);
  and a_nc_d (a_nc_d_out, d_ff_1_q, not_3_out, d_ff_4_q);
  and a_c_nd (a_c_nd_out, d_ff_1_q, d_ff_3_q, not_4_out);
  or or_3 (or_3_out, a_nc_d_out, a_c_nd_out, na_c_d_out);
  and na_c_d (na_c_d_out, not_1_out, d_ff_3_q, d_ff_4_q);
  and a_nc_nd (a_nc_nd_out, d_ff_1_q, not_3_out, not_4_out);
  and na_d (na_d_out, not_1_out, d_ff_4_q);
  or or_4 (or_4_out, a_nc_nd_out, na_d_out, na_c_out);
  and na_c (na_c_out, not_1_out, d_ff_3_q);

  // Notes on the sheet:
  //   Input/a
  //   Horloge
  //   N2
  //   N1
  //   E2/b
  //   E1/c
  //   E0/d
  //   N0
  //   N2
  //   N1
  //   N0
  //   Output
endmodule
